# Fritzing sketch allConnection (saved by Fritzing 0.9.3b)

parts:
  Part1 = Arduino Nano (Rev3.0)
  Part2 = InvenSense MPU6050
  R1 = Basic Flex Resistor
  R2 = Basic Flex Resistor
  R3 = Basic Flex Resistor
  R4 = Basic Flex Resistor
  R5 = Basic Flex Resistor
  Part3 = Bluetooth HC-05 Macho
  R7 = Resistor [tolerance=±5% resistance=220 package=THT]  # not connected
  R8 = Resistor [tolerance=±5% resistance=220 package=THT]  # not connected
  R9 = Resistor [tolerance=±5% resistance=220 package=THT]  # not connected
  R10 = Resistor [tolerance=±5% resistance=220 package=THT]  # not connected
  R11 = Resistor [tolerance=±5% resistance=220 package=THT]
  Raspberry_Pi_1 = Raspberry Pi 3 [part_number=RPI-3-V1.2]  # not connected
  R13 = Resistor [tolerance=±5% resistance=220 package=THT]
  R14 = Resistor [tolerance=±5% resistance=220 package=THT]

nets:
  N1: Part1.D1/TX, R13.Pin_0, R14.Pin_1
  N2: Part1.D0/RX, Part3.TXD
  GND: Part1.GND, Part2.GND, R1.Pin_2, R2.Pin_2, R3.Pin_2, R4.Pin_2, R5.Pin_2, Part3.GND
  N3: Part1.D2, Part2.INT
  5V: Part1.5V, Part2.VCC, R14.Pin_0
  N4: Part1.A6, Part2.SCL
  N5: Part1.A5, Part2.SDA
  N6: Part1.3V3, R1.pin_1, R2.pin_1, R3.pin_1, R4.pin_1, R5.pin_1, R11.Pin_1
  N7: Part3.RXD, R13.Pin_1
